// Logisim project lab4.4.circ as structural Verilog: 1 circuit, main circuit main
// 移位器
module main (
  input  [4:0] shamt,
  input  L_R,
  input  A_L,
  input  [31:0] DataIn,
  output [31:0] DataOut
);

  wire [1:0] LRAL;
  wire [7:0] multiplexer_6_out_2;
  wire [23:0] multiplexer_6_out;
  wire [31:0] multiplexer_1_out, multiplexer_2_out, multiplexer_3_out, multiplexer_4_out, multiplexer_5_out,
       multiplexer_7_out, multiplexer_8_out, multiplexer_9_out;

  not not_1 (LRAL[1], L_R);
  not not_2 (LRAL[0], A_L);
  Multiplexer #(.select(2), .width(32), .enable("false")) multiplexer_1 (
    .in0({DataIn[30:0], DataIn[31]}), .in1({DataIn[30:0], 1'b0}), .in2({{2{DataIn[31]}}, DataIn[30:1]}),
    .in3({1'b0, DataIn[31:1]}), .out(multiplexer_1_out), .sel(LRAL));
  Multiplexer #(.width(32), .enable("false")) multiplexer_2 (
    .in0(DataIn), .in1(multiplexer_1_out), .out(multiplexer_2_out), .sel(shamt[0]));
  Multiplexer #(.select(2), .width(32), .enable("false")) multiplexer_3 (
    .in0({multiplexer_2_out[29:0], multiplexer_2_out[31:30]}), .in1({multiplexer_2_out[29:0], 2'b00}),
    .in2({{3{multiplexer_2_out[31]}}, multiplexer_2_out[30:2]}), .in3({2'b00, multiplexer_2_out[31:2]}),
    .out(multiplexer_3_out), .sel(LRAL));
  Multiplexer #(.width(32), .enable("false")) multiplexer_4 (
    .in0(multiplexer_2_out), .in1(multiplexer_3_out), .out(multiplexer_4_out), .sel(shamt[1]));
  Multiplexer #(.select(2), .width(32), .enable("false")) multiplexer_5 (
    .in0({multiplexer_4_out[27:0], multiplexer_4_out[31:28]}), .in1({multiplexer_4_out[27:0], 4'b0000}),
    .in2({{5{multiplexer_4_out[31]}}, multiplexer_4_out[30:4]}), .in3({4'b0000, multiplexer_4_out[31:4]}),
    .out(multiplexer_5_out), .sel(LRAL));
  Multiplexer #(.width(32), .enable("false")) multiplexer_6 (
    .in0(multiplexer_4_out), .in1(multiplexer_5_out), .out({multiplexer_6_out_2, multiplexer_6_out}),
    .sel(shamt[2]));
  Multiplexer #(.select(2), .width(32), .enable("false")) multiplexer_7 (
    .in0({multiplexer_6_out, multiplexer_6_out_2}), .in1({multiplexer_6_out, {8{1'b0}}}),
    .in2({{9{multiplexer_6_out_2[7]}}, multiplexer_6_out_2[6:0], multiplexer_6_out[23:8]}),
    .in3({{8{1'b0}}, multiplexer_6_out_2, multiplexer_6_out[23:8]}), .out(multiplexer_7_out), .sel(LRAL));
  Multiplexer #(.width(32), .enable("false")) multiplexer_8 (
    .in0({multiplexer_6_out_2, multiplexer_6_out}), .in1(multiplexer_7_out), .out(multiplexer_8_out),
    .sel(shamt[3]));
  Multiplexer #(.select(2), .width(32), .enable("false")) multiplexer_9 (
    .in0({multiplexer_8_out[15:0], multiplexer_8_out[31:16]}), .in1({multiplexer_8_out[15:0], {16{1'b0}}}),
    .in2({{17{multiplexer_8_out[31]}}, multiplexer_8_out[30:16]}),
    .in3({{16{1'b0}}, multiplexer_8_out[31:16]}), .out(multiplexer_9_out), .sel(LRAL));
  Multiplexer #(.width(32), .enable("false")) multiplexer_10 (
    .in0(multiplexer_8_out), .in1(multiplexer_9_out), .out(DataOut), .sel(shamt[4]));

  // Other names for the same wires on the sheet: Din[31:0] = DataIn; Arth_Logic = A_L; Dout[31:0] = DataOut;
  //   Left_Right = L_R

  // Notes on the sheet:
  //   L/R,A/L: 00逻辑右移，01算术右移，10逻辑左移，11：循环左移
  //   输入引脚
  //   请勿修改引脚名称、电路名称及电路封装外观
  //   提示：使用多路选择器、逻辑门实现32位桶形移位器，禁止直接使用移位器组件。
  //   输出引脚
endmodule
