// Logisim project think1.circ as structural Verilog: 1 circuit, main circuit main
module main (
  input  CLK,
  input  [31:0] X,
  input  Reset,
  input  [31:0] Y
);

  wire LOAD, not_1_out, or_1_out, STOP;
  wire [0:0] adder_1_out_2;
  wire [7:0] counter_1_q;
  wire [30:0] adder_1_out;
  wire [31:0] multiplexer_1_out, multiplexer_2_out, Z1, Z2;
  wire [31:31] adder_1_cout;

  not not_1 (not_1_out, STOP);
  Multiplexer #(.width(32), .enable("false")) multiplexer_1 (
    .in0({32{1'b0}}), .in1(X), .out(multiplexer_1_out), .sel(Z2[0]));
  Register #(.width(32), .Select("low")) register_1 (
    .D({adder_1_cout[31], adder_1_out}), .en(not_1_out), .Q(Z1), .clk(CLK), .clr(Reset));
  Adder #(.width(32)) adder_1 (
    .a(multiplexer_1_out), .b(Z1), .out({adder_1_out, adder_1_out_2[0]}), .cin(1'b0), .cout(adder_1_cout[31]));
  Register #(.width(32), .Select("low")) u_Y (.D(multiplexer_2_out), .en(not_1_out), .Q(Z2), .clk(CLK), .clr(Reset));
  Multiplexer #(.width(32), .enable("false")) multiplexer_2 (
    .in0({adder_1_out_2[0], Z2[31:1]}), .in1(Y), .out(multiplexer_2_out), .sel(LOAD));
  or or_1 (or_1_out, Reset, not_1_out);
  Counter counter_1 (
    .load(1'b0), .D({8{1'b0}}), .count(or_1_out), .Q(counter_1_q), .clk(CLK), .clr(Reset), .down(1'b0));  // open: carry, preset
  Comparator #(.mode("unsigned")) comparator_1 (.a(counter_1_q), .b({8{1'b0}}), .eq(LOAD));  // open: gt, lt
  Comparator #(.mode("unsigned")) comparator_2 (.a(counter_1_q), .b(8'h21), .eq(STOP));  // open: gt, lt

  // Other names for the same wires on the sheet: RST = Reset

  // Notes on the sheet:
  //   P
endmodule
