// Logisim project lab5.2.circ as structural Verilog: 1 circuit, main circuit DataRam
// DataRAM
module DataRam (
  input  CLK,
  input  CLR,
  input  WE,
  input  [2:0] MemOp,
  input  [17:0] Addr,
  input  [31:0] Din,
  output AlignErr,
  output [31:0] DataOut
);

  wire and_1_out, and_2_out, and_3_out, and_4_out, and_5_out, and_6_out, and_7_out, and_8_out, and_9_out,
       and_11_out, and_12_out, and_13_out, and_14_out;
  wire [3:0] or_4_out;
  wire [4:0] bit_extender_1_out, bit_extender_2_out, bit_extender_3_out, bit_extender_4_out;
  wire [7:0] multiplexer_1_out, ram_1_data, ram_2_data, ram_3_data, ram_4_data, shifter_2_out, shifter_4_out,
       shifter_6_out, shifter_8_out;
  wire [15:0] multiplexer_2_out;
  wire [17:0] adder_1_out, adder_2_out, adder_3_out, adder_4_out, adder_5_out, adder_6_out, shifter_1_out,
       shifter_3_out, shifter_5_out, shifter_7_out;
  wire [31:0] bit_extender_5_out, bit_extender_6_out, bit_extender_7_out, bit_extender_8_out;
  wire [31:8] shifter_2_out_2, shifter_4_out_2, shifter_6_out_2, shifter_8_out_2;

  and and_1 (and_1_out, ~MemOp[2], ~MemOp[1], ~MemOp[0], ~Addr[1], ~Addr[0]);  // AND_Gate
  and and_2 (and_2_out, ~MemOp[1], MemOp[0], Addr[1], Addr[0]);  // AND_Gate
  and and_3 (and_3_out, MemOp[1], ~MemOp[0], Addr[1], ~Addr[0]);  // AND_Gate
  and and_4 (and_4_out, ~MemOp[1], MemOp[0], Addr[1], ~Addr[0]);  // AND_Gate
  and and_5 (and_5_out, MemOp[1], ~MemOp[0], Addr[1], ~Addr[0]);  // AND_Gate
  and and_6 (and_6_out, ~MemOp[1], MemOp[0], ~Addr[1], Addr[0]);  // AND_Gate
  and and_7 (and_7_out, MemOp[1], ~MemOp[0], ~Addr[1], ~Addr[0]);  // AND_Gate
  and and_8 (and_8_out, ~MemOp[1], MemOp[0], ~Addr[1], ~Addr[0]);  // AND_Gate
  and and_9 (and_9_out, MemOp[1], ~MemOp[0], ~Addr[1], ~Addr[0]);  // AND_Gate
  or or_1 (or_4_out[3], and_1_out, and_2_out, and_3_out);
  or or_2 (or_4_out[2], and_1_out, and_4_out, and_5_out);
  or or_3 (or_4_out[1], and_1_out, and_6_out, and_7_out);
  or or_4 (or_4_out[0], and_1_out, and_8_out, and_9_out);
  and and_10 (AlignErr, ~or_4_out[3], ~or_4_out[2], ~or_4_out[1], ~or_4_out[0]);  // AND_Gate
  Adder #(.width(18)) adder_1 (.a({18{1'b0}}), .b({18{1'b0}}), .out(adder_1_out), .cin(or_4_out[0]));  // open: cout
  Adder #(.width(18)) adder_2 (.a({18{1'b0}}), .b(adder_1_out), .out(adder_2_out), .cin(or_4_out[1]));  // open: cout
  Bit_Extender #(.in_width(18), .out_width(5), .\type ("zero")) bit_extender_1 (
    .in(shifter_1_out), .out(bit_extender_1_out));
  Shifter #(.width(18)) shifter_1 (.in(adder_3_out), .\dist (5'b00011), .out(shifter_1_out));
  and and_11 (and_11_out, or_4_out[3], WE);
  Adder #(.width(18)) adder_3 (.a({18{1'b0}}), .b(adder_2_out), .out(adder_3_out), .cin(or_4_out[2]));  // open: cout
  Shifter #(.width(32), .shift("lr")) shifter_2 (
    .in(Din), .\dist (bit_extender_1_out), .out({shifter_2_out_2, shifter_2_out}));
  RAM #(.addrWidth(18), .bus("separate"), .Select("high")) ram_1 (
    .addr({2'b00, Addr[17:2]}), .din(shifter_2_out), .data(ram_1_data), .str(and_11_out), .sel(or_4_out[3]),
    .clk(CLK), .clr(CLR));  // open: ld
  Adder #(.width(18)) adder_4 (.a({18{1'b0}}), .b({18{1'b0}}), .out(adder_4_out), .cin(or_4_out[0]));  // open: cout
  Adder #(.width(18)) adder_5 (.a({18{1'b0}}), .b(adder_4_out), .out(adder_5_out), .cin(or_4_out[1]));  // open: cout
  Shifter #(.width(18)) shifter_3 (.in(adder_5_out), .\dist (5'b00011), .out(shifter_3_out));
  Bit_Extender #(.in_width(18), .out_width(5), .\type ("zero")) bit_extender_2 (
    .in(shifter_3_out), .out(bit_extender_2_out));
  and and_12 (and_12_out, or_4_out[2], WE);
  Shifter #(.width(32), .shift("lr")) shifter_4 (
    .in(Din), .\dist (bit_extender_2_out), .out({shifter_4_out_2, shifter_4_out}));
  RAM #(.addrWidth(18), .bus("separate"), .Select("high")) ram_2 (
    .addr({2'b00, Addr[17:2]}), .din(shifter_4_out), .data(ram_2_data), .str(and_12_out), .sel(or_4_out[2]),
    .clk(CLK), .clr(CLR));  // open: ld
  Adder #(.width(18)) adder_6 (.a({18{1'b0}}), .b({18{1'b0}}), .out(adder_6_out), .cin(or_4_out[0]));  // open: cout
  Shifter #(.width(18)) shifter_5 (.in(adder_6_out), .\dist (5'b00011), .out(shifter_5_out));
  Bit_Extender #(.in_width(18), .out_width(5), .\type ("zero")) bit_extender_3 (
    .in(shifter_5_out), .out(bit_extender_3_out));
  and and_13 (and_13_out, or_4_out[1], WE);
  Shifter #(.width(32), .shift("lr")) shifter_6 (
    .in(Din), .\dist (bit_extender_3_out), .out({shifter_6_out_2, shifter_6_out}));
  RAM #(.addrWidth(18), .bus("separate"), .Select("high")) ram_3 (
    .addr({2'b00, Addr[17:2]}), .din(shifter_6_out), .data(ram_3_data), .str(and_13_out), .sel(or_4_out[1]),
    .clk(CLK), .clr(CLR));  // open: ld
  Shifter #(.width(18)) shifter_7 (.in({18{1'b0}}), .\dist (5'b00011), .out(shifter_7_out));
  Bit_Extender #(.in_width(18), .out_width(5), .\type ("zero")) bit_extender_4 (
    .in(shifter_7_out), .out(bit_extender_4_out));
  and and_14 (and_14_out, or_4_out[0], WE);
  Shifter #(.width(32), .shift("lr")) shifter_8 (
    .in(Din), .\dist (bit_extender_4_out), .out({shifter_8_out_2, shifter_8_out}));
  RAM #(.addrWidth(18), .bus("separate"), .Select("high")) ram_4 (
    .addr({2'b00, Addr[17:2]}), .din(shifter_8_out), .data(ram_4_data), .str(and_14_out), .sel(or_4_out[0]),
    .clk(CLK), .clr(CLR));  // open: ld
  Multiplexer #(.select(4), .width(8), .enable("false")) multiplexer_1 (
    .in1(ram_4_data), .in2(ram_3_data), .in4(ram_2_data), .in8(ram_1_data), .out(multiplexer_1_out),
    .sel(or_4_out));  // open: in0, in3, in5, in6, in7, in9, in10, in11, in12, in13, in14, in15
  Multiplexer #(.select(4), .width(16), .enable("false")) multiplexer_2 (
    .in3({ram_3_data, ram_4_data}), .in12({ram_1_data, ram_2_data}), .out(multiplexer_2_out), .sel(or_4_out));  // open: in0, in1, in2, in4, in5, in6, in7, in8, in9, in10, in11, in13, in14, in15
  assign bit_extender_5_out = {{24{1'b0}}, multiplexer_1_out};  // Bit_Extender bit_extender_5
  assign bit_extender_6_out = {{24{multiplexer_1_out[7]}}, multiplexer_1_out};  // Bit_Extender bit_extender_6
  assign bit_extender_7_out = {{16{1'b0}}, multiplexer_2_out};  // Bit_Extender bit_extender_7
  assign bit_extender_8_out = {{16{multiplexer_2_out[15]}}, multiplexer_2_out};  // Bit_Extender bit_extender_8
  Multiplexer #(.select(3), .width(32), .enable("false")) multiplexer_3 (
    .in0({ram_1_data, ram_2_data, ram_3_data, ram_4_data}), .in1(bit_extender_5_out),
    .in2(bit_extender_7_out), .in5(bit_extender_6_out), .in6(bit_extender_8_out), .out(DataOut), .sel(MemOp));  // open: in3, in4, in7

  // Other names for the same wires on the sheet: Dout[31:0] = DataOut

  // Notes on the sheet:
  //   输入引脚
  //   请勿修改引脚名称、电路名称及电路封装外观
  //   为了后续实验中的引用，不要修改MemOp的编码定义、引脚名称和在布局中的位置。
  //   32位数据存储器，按字节分4片存储，可按照字节、半字和字进行存储；读取字节或半字时，支持0扩展和符号位扩展。
  //   输出引脚
endmodule
