// Logisim project lab6.1.circ as structural Verilog: 1 circuit, main circuit 控制器
module \控制器  (
  input  [6:0] opcode,
  input  [2:0] funct3,
  input  [6:0] funct7,
  output [2:0] ExtOp,
  output RegWr,
  output [2:0] BandJ,
  output ALUASrc,
  output [1:0] ALUBSrc,
  output [3:0] ALUctr,
  output MemtoReg,
  output [2:0] MemOp,
  output MemWr
);

  wire and_1_out, and_3_out, and_4_out, and_5_out, and_6_out, and_7_out, and_8_out, and_9_out, and_10_out,
       and_11_out, and_12_out, and_13_out, and_14_out, and_15_out, and_17_out, and_20_out, and_21_out,
       and_22_out, and_23_out, and_24_out, and_25_out, and_26_out, and_27_out, and_28_out, comparator_1_eq,
       comparator_2_eq, comparator_3_eq, comparator_4_eq;
  wire [2:0] multiplexer_1_out;

  and and_1 (and_1_out, ~opcode[6], opcode[5], opcode[4], ~opcode[3], ~opcode[2], opcode[1], opcode[0]);  // AND_Gate
  and and_2 (ExtOp[2], opcode[6], opcode[5], ~opcode[4], opcode[3], opcode[2], opcode[1], opcode[0]);  // AND_Gate
  and and_3 (and_3_out, ~opcode[6], ~opcode[5], opcode[4], ~opcode[3], ~opcode[2], opcode[1], opcode[0]);  // AND_Gate
  and and_4 (and_4_out, ~opcode[6], opcode[5], ~opcode[4], ~opcode[3], ~opcode[2], opcode[1], opcode[0]);  // AND_Gate
  Comparator #(.width(7)) comparator_1 (.a(opcode), .b(7'b0110111), .eq(comparator_1_eq));  // open: gt, lt
  Comparator #(.width(7)) comparator_2 (.a(opcode), .b(7'b0010011), .eq(comparator_2_eq));  // open: gt, lt
  Comparator #(.width(7)) comparator_3 (.a(opcode), .b(7'b0110011), .eq(comparator_3_eq));  // open: gt, lt
  Comparator #(.width(7)) comparator_4 (.a(opcode), .b(7'b1100011), .eq(comparator_4_eq));  // open: gt, lt
  and and_5 (and_5_out, ~opcode[6], opcode[5], opcode[4], ~opcode[3], opcode[2], opcode[1], opcode[0]);  // AND_Gate
  and and_6 (and_6_out, opcode[6], opcode[5], ~opcode[4], ~opcode[3], ~opcode[2], opcode[1], opcode[0]);  // AND_Gate
  and and_7 (and_7_out, comparator_2_eq, funct3[2], ~funct3[1], funct3[0], funct7[5]);  // AND_Gate
  and and_8 (and_8_out, comparator_3_eq, funct7[5]);
  and and_9 (and_9_out, comparator_2_eq, funct3[2]);
  and and_10 (and_10_out, comparator_3_eq, funct3[2]);
  and and_11 (and_11_out, comparator_2_eq, funct3[1]);
  and and_12 (and_12_out, comparator_3_eq, funct3[1]);
  and and_13 (and_13_out, comparator_2_eq, funct3[0]);
  and and_14 (and_14_out, comparator_3_eq, funct3[0]);
  and and_15 (and_15_out, comparator_4_eq, funct3[1]);
  and and_16 (MemtoReg, ~opcode[6], ~opcode[5], ~opcode[4], ~opcode[3], ~opcode[2], opcode[1], opcode[0]);  // AND_Gate
  and and_17 (and_17_out, ~opcode[6], 1'b1, opcode[4], ~opcode[3], opcode[2], opcode[1], opcode[0]);  // AND_Gate
  or or_1 (ALUctr[3], comparator_1_eq, and_7_out, and_8_out);
  or or_2 (ALUctr[2], comparator_1_eq, and_9_out, and_10_out);
  or or_3 (ALUctr[1], comparator_1_eq, and_11_out, and_12_out, comparator_4_eq);
  or or_4 (ALUctr[0], comparator_1_eq, and_13_out, and_14_out, and_15_out);
  and and_18 (MemWr, ~opcode[6], opcode[5], ~opcode[4], ~opcode[3], ~opcode[2], opcode[1], opcode[0]);  // AND_Gate
  or or_5 (ExtOp[1], and_6_out, and_4_out);
  or or_6 (ExtOp[0], and_17_out, and_6_out);
  and and_19 (BandJ[2], opcode[6], opcode[5], ~opcode[4], ~opcode[3], ~opcode[2], opcode[1], opcode[0]);  // AND_Gate
  and and_20 (and_20_out, opcode[6], opcode[5], ~opcode[4], opcode[3], opcode[2], opcode[1], opcode[0]);  // AND_Gate
  and and_21 (and_21_out, opcode[6], opcode[5], ~opcode[4], ~opcode[3], opcode[2], opcode[1], opcode[0]);  // AND_Gate
  and and_22 (and_22_out, ~opcode[6], ~opcode[5], opcode[4], ~opcode[3], opcode[2], opcode[1], opcode[0]);  // AND_Gate
  or or_7 (ALUBSrc[0], and_21_out, and_20_out);
  and and_23 (and_23_out, ~opcode[6], 1'b1, ~opcode[4], ~opcode[3], ~opcode[2], opcode[1], opcode[0]);  // AND_Gate
  and and_24 (and_24_out, ~opcode[6], ~opcode[5], opcode[4], ~opcode[3], 1'b1, opcode[1], opcode[0]);  // AND_Gate
  and and_25 (and_25_out, opcode[0], opcode[1], ~opcode[2], ~opcode[3], ~opcode[4], 1'b1, ~opcode[6]);  // AND_Gate
  Multiplexer #(.select(3), .width(3), .enable("false")) multiplexer_1 (
    .in0(3'b101), .in1(3'b110), .in2(3'b000), .in3(3'b000), .in4(3'b001), .in5(3'b010), .in6(3'b000),
    .in7(3'b000), .out(multiplexer_1_out), .sel(funct3));
  and and_26 (and_26_out, ~opcode[6], opcode[5], opcode[4], ~opcode[3], opcode[2], opcode[1], opcode[0]);  // AND_Gate
  or or_8 (RegWr, and_5_out, and_1_out, and_3_out, and_22_out, MemtoReg, and_20_out, and_21_out);
  or or_9 (BandJ[1], and_21_out, and_27_out);
  and and_27 (and_27_out, funct3[2], BandJ[2]);
  and and_28 (and_28_out, BandJ[2], funct3[0]);
  or or_10 (BandJ[0], and_28_out, and_20_out);
  or or_11 (ALUASrc, and_22_out, ALUBSrc[0]);
  or or_12 (ALUBSrc[1], and_26_out, and_24_out, and_23_out);
  and and_29 (MemOp[0], multiplexer_1_out[0], and_25_out);
  and and_30 (MemOp[1], and_25_out, multiplexer_1_out[1]);
  and and_31 (MemOp[2], and_25_out, multiplexer_1_out[2]);

  // Notes on the sheet:
  //   输入引脚
  //   请勿修改引脚名称、电路名称及电路封装外观
  //   提示：根据指令种类，把7位指令code用一位指令类型标志位来表示，再通过功能码来区分具体指令，生成控制信号。
  //   输出引脚
endmodule
